# Fritzing sketch blind shoes (saved by Fritzing 0.9.3b)
circuit board: 37.637cm x 17.5003cm
breadboards: 1

parts:
  Part1 = Arduino Uno (Rev3) - ICSP
  J1 = Piezo Speaker
  U1 = LCD-16X2 [package=lcd-16x2_noholes]
  R1 = Resistor [tolerance=±5% power=0.25 resistance=220 package=THT]
  Gizwits_WiFi_Witty_ESP-12F1 = Gizwits WiFi Witty ESP-12F
  Part2 = Soil Moisture Sensor
  HC-SR04_Sensor_3 = HC-SR04 Ultrasonic Distance Sensor

nets:
  N1: Part1.A0, HC-SR04_Sensor_3.TRIG
  N2: Part1.A4/SDA, J1.pin2
  N3: Part1.A5/SCL, HC-SR04_Sensor_3.ECHO
  N4: Part1.D8, U1.RS
  N5: Part1.D9_PWM, U1.E
  N6: Part1.D10_PWM/SS, U1.DB4
  N7: Part1.D11_PWM/MOSI, U1.DB5
  N8: Part1.D12/MISO, U1.DB6
  N9: Part1.D13/SCK, U1.DB7
  N10: Part1.D3_PWM, Gizwits_WiFi_Witty_ESP-12F1.RXD
  N11: Part1.D4, Part2.SIG
  GND: J1.pin1, U1.VSS, U1.R_W, U1.K, R1.Pin_1, Gizwits_WiFi_Witty_ESP-12F1.GND, Part2.GND
  VCC: U1.VDD, Gizwits_WiFi_Witty_ESP-12F1.VCC, Part2.VCC
  N12: U1.VO, R1.Pin_0

// code stored in the sketch: Untitled.ino
#include <SoftwareSerial.h> 
SoftwareSerial gps(6, 7);// rx tx
#define trigPin3 A0
#define echoPin3 A1
#define trigPin2 2
#define echoPin2 3
#define trigPin1 A4
#define echoPin1 A5
#define trigPin4 A2
#define echoPin4 A3

#define buzzer 9
#define button 4
int but=0,aag=0,mois=0;
long duration, distance,sensor1,sensor2,sensor3,sensor4; 
char str[70];
int temp=0,i;  
boolean Serial_status=0;

void setup()
{
  gps.begin(9600);
  Serial.begin(9600);
  pinMode(trigPin1, OUTPUT);
  pinMode(echoPin1, INPUT);
  pinMode(trigPin2, OUTPUT);
  pinMode(echoPin2, INPUT);
  pinMode(trigPin3, OUTPUT);
  pinMode(echoPin3, INPUT);
  pinMode(trigPin4, OUTPUT);
  pinMode(echoPin4, INPUT);
  pinMode(buzzer, OUTPUT);
  pinMode(button,INPUT_PULLUP);
} 
void loop()
{
  but=digitalRead(button);
  if(but==LOW)
  {
   tracking();
  }  
  ultrasensor(trigPin1, echoPin1);
  sensor1 = distance;
  delay(2); 
  ultrasensor(trigPin2, echoPin2);
  sensor2 = distance;
  delay(2); 
  ultrasensor(trigPin3, echoPin3);
  sensor3 = distance;
  delay(2); 
  ultrasensor(trigPin4, echoPin4);
  sensor4 = distance;
  delay(2); 
  
  Serial.print("sensor1=");
  Serial.println(sensor1);
  Serial.print("sensor2=");
  Serial.println(sensor2);
  Serial.print("sensor3=");
  Serial.println(sensor3);
  Serial.print("sensor4=");
  Serial.println(sensor4);
  if(sensor1 <= 30 && sensor1 >= 2)
  {
  gps.println("obstacle in left");
  beep1();
  } 
  else if(sensor2 <= 30 && sensor1 >= 2)
  {
   gps.println("obstacle in right");
   beep2();
  }
   else if(sensor3 <22)
  {
   if(sensor4 > 27 )
  {
   gps.println("obstacle in right");
   beep2();
  } 
  }
  delay(10);       
}
 void init_sms()
 {
  Serial.println("AT+CMGF=1");
  delay(400);
  Serial.println("AT+CMGS=\"+918700828620\"");   // use your 10 digit cell no. here
  delay(400);
 }void init_sms1()
 {
  Serial.println("AT+CMGF=1");
  delay(400);
  Serial.println("AT+CMGS=\"+917054577507\"");   // use your 10 digit cell no. here
  delay(400);
 }
void send_data(String message)
{
  Serial.println(message);
  delay(200);
}
void send_sms()
{
  Serial.write(26);
}
void tracking()
{
  digitalWrite(buzzer,HIGH);
  init_sms();
   send_data("PLEASE HELP ME. My Location is:\n");
    send_data("28.6297338N,77.3698669E");
    //send_data("https://goo.gl/maps/P92TDYFxsJab1k647");
    send_sms();
    delay(4000);
     init_sms();
    send_data("PLEASE HELP ME. My Location is:\n");
     send_data("28.6297338N,77.3698669E");
    //send_data("https://goo.gl/maps/P92TDYFxsJab1k647");
    send_sms();
    delay(5000);
    digitalWrite(buzzer,LOW);
}
void ultrasensor(int trigPin,int echoPin)
{
  
 digitalWrite(trigPin, LOW);  // Added this line
 delayMicroseconds(2); // Added this line
 digitalWrite(trigPin, HIGH);
 delayMicroseconds(10); // Added this line
 digitalWrite(trigPin, LOW);
 duration = pulseIn(echoPin, HIGH);
 distance = (duration/2) / 29.1;
}
void beep1()
{
 digitalWrite(buzzer,HIGH);
 delay(50);
 digitalWrite(buzzer,LOW);
 delay(20);
}
void beep2()
{
 digitalWrite(buzzer,HIGH);
 delay(100);
 digitalWrite(buzzer,LOW);
 delay(50);
}
void beep3()
{
 digitalWrite(buzzer,HIGH);
 delay(300);
 digitalWrite(buzzer,LOW);
 delay(100);
}
